# Fritzing sketch Pong (saved by Fritzing 0.9.3b)
breadboards: 1

parts:
  Parte1 = Arduino Uno (Rev3) - ICSP
  Grove1 = Grove OLED 128x96
  Parte2 = Thumb Joystick

nets:
  N1: Parte1.A0, Parte2.VERT
  N2: Parte1.A1, Parte2.HORZ
  N3: Parte1.A2, Parte2.SEL
  N4: Parte1.A4/SDA, Grove1.SDA
  N5: Parte1.A5/SCL, Grove1.SCL
  VCC: Parte1.5V, Grove1.VCC, Parte2.VCC
  GND: Parte1.GND, Grove1.GND, Parte2.GND
